# Fritzing sketch 回路図 (saved by Fritzing 0.9.3b)
breadboards: 1

parts:
  U1 = ESP-WROOM-02-AE [part_number=ESP-WROOM-02-AE]
  Debugger1 = Debugger
  R1 = Resistor [tolerance=±5% resistance=10k package=THT]
  J1 = Basic Force Sensing Resistor (FSR) [package=THT]
  J2 = Basic Servo
  VCC1 = Battery
  S3 = Pushbutton [package="[THT]"]
  R2 = Resistor [tolerance=±5% resistance=10k package=THT]
  R3 = Resistor [tolerance=±5% resistance=10k package=THT]
  R4 = Resistor [tolerance=±5% resistance=220 package=THT]
  R5 = Resistor [tolerance=±5% resistance=220 package=THT]
  S4 = Pushbutton [package="[THT]"]

nets:
  3V3: U1.3V3, U1.EN, R1.Pin_0, J1.pin_1, J2.vcc, VCC1.+, R2.Pin_0
  N1: U1.IO15, R3.Pin_0
  N2: U1.IO2, R2.Pin_1
  N3: U1.IO0, R1.Pin_1, S3.Pin_3, S3.Pin_4
  GND: U1.GND, Debugger1.GND, J2.gnd, VCC1.-, S3.Pin_1, S3.Pin_2, R3.Pin_1, R4.Pin_1, R5.Pin_1, S4.Pin_3, S4.Pin_4
  N4: U1.TOUT, J1.pin_0, R4.Pin_0, R5.Pin_0
  N5: U1.IO5, S4.Pin_1, S4.Pin_2
  N6: U1.TXD, Debugger1.RX
  N7: U1.RXD, Debugger1.TX
  N8: U1.IO4, J2.pulse

custom parts:
  ESP-WROOM-02-AE: ESP-WROOM-02 with the DIP breakout board by Akizuki-Electronics in Japan. See http://akizukidenshi.com/catalog/g/gK-09758/ for the detauls.
